// Logisim project sentinela.circ as structural Verilog: 6 circuits, main circuit main
module main (
  input  [7:0] x_in
);

  wire ack_d, ackp, alarme_o, btn_ack, btn_start, clk, corte_o, dne, falha_o, hold, multiplexer_1_out,
       multiplexer_2_out, ndne, nprev, prev, rst, start, vent_o;
  wire [3:0] c_hi, c_lo;
  wire [7:0] y;

  Clock u_clk (.out(clk));
  Button u_start (.out(btn_start));
  Button ack (.out(btn_ack));
  Button u_rst (.out(rst));
  Multiplexer #(.width(1)) multiplexer_1 (.in0(btn_start), .in1(1'b0), .out(multiplexer_1_out), .sel(rst));
  not not_1 (nprev, prev);
  and and_1 (start, btn_start, nprev);
  not not_2 (ndne, dne);
  and and_2 (hold, ackp, ndne);
  or or_1 (ack_d, btn_ack, hold);
  Multiplexer #(.width(1)) multiplexer_2 (.in0(ack_d), .in1(1'b0), .out(multiplexer_2_out), .sel(rst));
  Register #(.width(1)) reg_prev (.D(multiplexer_1_out), .Q(prev), .clk(clk));  // open: en, clr
  Register #(.width(1)) reg_ackp (.D(multiplexer_2_out), .Q(ackp), .clk(clk));  // open: en, clr
  sentinela_core sentinela_core_1 (
    .x_in(x_in), .start(start), .ack(ackp), .clk(clk), .rst(rst), .y_out(y), .done(dne),
    .ciclos({c_hi, c_lo}), .vent(vent_o), .alarme(alarme_o), .corte(corte_o), .falha_sensor(falha_o));
  Hex_Digit_Display hex_digit_display_1 (.value(y[7:4]));  // open: dp
  LED ventilacao (.in(vent_o));
  LED alarme (.in(alarme_o));
  LED corte (.in(corte_o));
  LED falha_sensor (.in(falha_o));
  LED done (.in(dne));
  Hex_Digit_Display hex_digit_display_2 (.value(y[3:0]));  // open: dp
  Hex_Digit_Display hex_digit_display_3 (.value(c_hi));  // open: dp
  Hex_Digit_Display hex_digit_display_4 (.value(c_lo));  // open: dp

  // Other names for the same wires on the sheet: cic[7:0] = {c_hi, c_lo}; y_lo[3:0] = y[3:0]; y_hi[3:0] = y[7:4]

  // Notes on the sheet:
  //   y_out
  //   ciclos
endmodule

module alu8 (
  input  [7:0] a,
  input  [7:0] b,
  input  [1:0] op,
  output [7:0] y,
  output zero,
  output carry
);

  wire c_add, c_sub;
  wire [7:0] s_add, s_and, s_sub;

  Adder #(.width(8)) adder_1 (.a(a), .b(b), .out(s_add), .cin(1'b0), .cout(c_add));
  Subtractor #(.width(8)) subtractor_1 (.a(a), .b(b), .out(s_sub), .bin(1'b0), .bout(c_sub));
  assign s_and = a & b;  // AND_Gate and_1, 8 bits wide
  Multiplexer #(.width(8), .select(2)) multiplexer_1 (
    .in0(s_add), .in1(s_sub), .in2(s_and), .in3({1'b0, a[7:1]}), .out(y), .sel(op));
  Multiplexer #(.width(1), .select(2)) multiplexer_2 (
    .in0(c_add), .in1(c_sub), .in2(1'b0), .in3(a[0]), .out(carry), .sel(op));
  Comparator #(.width(8), .mode("unsigned")) comparator_1 (.a(y), .b({8{1'b0}}), .eq(zero));  // open: gt, lt

  // Other names for the same wires on the sheet: s_shr[6:0] = a[7:1]
endmodule

module regs2 (
  input  [7:0] din,
  input  we,
  input  sel,
  input  clk,
  input  rst,
  output [7:0] r0_out,
  output [7:0] r1_out
);

  wire and_1_out, and_2_out, not_1_out, or_1_out, or_2_out;
  wire [7:0] d;

  Multiplexer #(.width(8)) multiplexer_1 (.in0(din), .in1({8{1'b0}}), .out(d), .sel(rst));
  and and_1 (and_1_out, we, not_1_out);
  not not_1 (not_1_out, sel);
  and and_2 (and_2_out, we, sel);
  Register #(.width(8)) r0 (.D(d), .en(or_1_out), .Q(r0_out), .clk(clk));  // open: clr
  or or_1 (or_1_out, and_1_out, rst);
  Register #(.width(8)) r1 (.D(d), .en(or_2_out), .Q(r1_out), .clk(clk));  // open: clr
  or or_2 (or_2_out, and_2_out, rst);
endmodule

module fir4 (
  input  [7:0] x_in,
  input  start,
  input  clk,
  input  rst,
  output [7:0] y_out,
  output done,
  output [7:0] ciclos
);

  wire c_lo, en_acc, en_y, go, idle, last, mac, n0, n1, nlast, rgo, t1;
  wire [1:0] i, i_next, multiplexer_7_out, multiplexer_10_out, ns, s;
  wire [7:0] c_lo8, cyc_base, cyc_next, h, multiplexer_2_out, multiplexer_3_out, multiplexer_4_out,
       multiplexer_5_out, multiplexer_8_out, multiplexer_9_out, p_hi, p_lo, s_h1, s_hi, s_lo, x0, x1, x2, x3,
       x_sel;
  wire [15:0] acc, multiplexer_6_out;

  not not_1 (n0, s[0]);
  not not_2 (n1, s[1]);
  and and_1 (idle, n1, n0);
  and and_2 (mac, n1, s[0]);
  and and_3 (done, s[1], n0);
  and and_4 (last, i[0], i[1]);
  not not_3 (nlast, last);
  and and_5 (go, idle, start);
  and and_6 (t1, mac, nlast);
  or or_1 (ns[0], go, t1);
  and and_7 (ns[1], mac, last);
  or or_2 (rgo, rst, go);
  or or_3 (en_acc, rgo, mac);
  or or_4 (en_y, rst, ns[1]);
  Adder #(.width(2)) adder_1 (.a(i), .b(2'b01), .out(i_next), .cin(1'b0));  // open: cout
  Multiplexer #(.width(8)) multiplexer_1 (.in0(ciclos), .in1({8{1'b0}}), .out(cyc_base), .sel(go));
  Adder #(.width(8)) adder_2 (.a(cyc_base), .b(8'h1), .out(cyc_next), .cin(1'b0));  // open: cout
  Multiplexer #(.width(8)) multiplexer_2 (.in0(x_in), .in1({8{1'b0}}), .out(multiplexer_2_out), .sel(rst));
  Register #(.width(8)) reg_x0 (.D(multiplexer_2_out), .en(rgo), .Q(x0), .clk(clk));  // open: clr
  Multiplexer #(.width(8)) multiplexer_3 (.in0(x0), .in1({8{1'b0}}), .out(multiplexer_3_out), .sel(rst));
  Register #(.width(8)) reg_x1 (.D(multiplexer_3_out), .en(rgo), .Q(x1), .clk(clk));  // open: clr
  Multiplexer #(.width(8)) multiplexer_4 (.in0(x1), .in1({8{1'b0}}), .out(multiplexer_4_out), .sel(rst));
  Register #(.width(8)) reg_x2 (.D(multiplexer_4_out), .en(rgo), .Q(x2), .clk(clk));  // open: clr
  Multiplexer #(.width(8)) multiplexer_5 (.in0(x2), .in1({8{1'b0}}), .out(multiplexer_5_out), .sel(rst));
  Register #(.width(8)) reg_x3 (.D(multiplexer_5_out), .en(rgo), .Q(x3), .clk(clk));  // open: clr
  Multiplexer #(.width(16)) multiplexer_6 (.in0({s_hi, s_lo}), .in1({16{1'b0}}), .out(multiplexer_6_out), .sel(rgo));
  Register #(.width(16)) reg_acc (.D(multiplexer_6_out), .en(en_acc), .Q(acc), .clk(clk));  // open: clr
  Multiplexer #(.width(2)) multiplexer_7 (.in0(i_next), .in1(2'b00), .out(multiplexer_7_out), .sel(rgo));
  Register #(.width(2)) reg_i (.D(multiplexer_7_out), .en(en_acc), .Q(i), .clk(clk));  // open: clr
  Multiplexer #(.width(8)) multiplexer_8 (
    .in0({s_hi[6:0], s_lo[7]}), .in1({8{1'b0}}), .out(multiplexer_8_out), .sel(rst));
  Register #(.width(8)) reg_y (.D(multiplexer_8_out), .en(en_y), .Q(y_out), .clk(clk));  // open: clr
  Multiplexer #(.width(8)) multiplexer_9 (.in0(cyc_next), .in1({8{1'b0}}), .out(multiplexer_9_out), .sel(rst));
  Register #(.width(8)) reg_ciclos (.D(multiplexer_9_out), .en(en_acc), .Q(ciclos), .clk(clk));  // open: clr
  Multiplexer #(.width(2)) multiplexer_10 (.in0(ns), .in1(2'b00), .out(multiplexer_10_out), .sel(rst));
  Register #(.width(2)) reg_s (.D(multiplexer_10_out), .Q(s), .clk(clk));  // open: en, clr
  ROM #(.addrWidth(2), .dataWidth(8)) rom_1 (.addr(i), .data(h));
  Multiplexer #(.width(8), .select(2)) multiplexer_11 (.in0(x0), .in1(x1), .in2(x2), .in3(x3), .out(x_sel), .sel(i));
  alu8 alu8_1 (.a(acc[7:0]), .b(p_lo), .op(2'b00), .y(s_lo), .carry(c_lo));  // open: zero
  alu8 alu8_2 (.a(acc[15:8]), .b(p_hi), .op(2'b00), .y(s_h1));  // open: zero, carry
  assign c_lo8 = {{7{1'b0}}, c_lo};  // Bit_Extender bit_extender_1
  alu8 alu8_3 (.a(s_h1), .b(c_lo8), .op(2'b00), .y(s_hi));  // open: zero, carry
  Multiplier #(.width(8)) multiplier_1 (.a(x_sel), .b(h), .out(p_lo), .cin({8{1'b0}}), .cout(p_hi));

  // Other names for the same wires on the sheet: acc_lo[7:0] = acc[7:0]; acc_hi[7:0] = acc[15:8]; dne = done;
  //   soma[15:0] = {s_hi, s_lo}; y_n[7:0] = {s_hi[6:0], s_lo[7]}; y[7:0] = y_out

  // Notes on the sheet:
  //   contents of rom_1 (hex, n*v repeats v):
  //   10 30 30 10
endmodule

module intertravamento (
  input  [7:0] temp,
  input  amostra_ok,
  input  ack,
  input  clk,
  input  rst,
  output vent,
  output alarme,
  output corte,
  output falha_sensor
);

  wire a1, a2, c_hold, congelado, en_amostra, en_s, f_hold, faixa, ge_c, ge_v, igual, inval, is_a, is_c,
       is_f, is_n, is_v, lt_c, lt_v, n0, n1, n2, nack, nsf, nv, nva, o1, o2, o3, o10, run_max, sf, t_a, t_f,
       t_n, va, va_c, vgc, x1;
  wire [1:0] s;
  wire [2:0] multiplexer_4_out, nxt, run_lo, s_d;
  wire [3:0] multiplexer_6_out, run, run_inc, run_sat;
  wire [7:0] anterior, multiplexer_5_out;

  Comparator #(.width(8), .mode("unsigned")) comparator_1 (.a(temp), .b(8'hb4), .lt(lt_v));  // open: gt, eq
  Comparator #(.width(8), .mode("unsigned")) comparator_2 (.a(temp), .b(8'hd2), .lt(lt_c));  // open: gt, eq
  Comparator #(.width(8), .mode("unsigned")) comparator_3 (.a(temp), .b(8'hf0), .gt(faixa));  // open: eq, lt
  Comparator #(.width(8), .mode("unsigned")) comparator_4 (.a(temp), .b(anterior), .eq(igual));  // open: gt, lt
  Adder #(.width(4)) adder_1 (.a(run), .b(4'b0001), .out(run_inc), .cin(1'b0), .cout(run_max));
  Multiplexer #(.width(4)) multiplexer_1 (.in0(run_inc), .in1(run), .out(run_sat), .sel(run_max));
  Multiplexer #(.width(4)) multiplexer_2 (.in0(4'b0001), .in1(run_sat), .out({congelado, run_lo}), .sel(igual));
  not not_1 (ge_v, lt_v);
  not not_2 (ge_c, lt_c);
  or or_1 (sf, faixa, congelado);
  not not_3 (nsf, sf);
  not not_4 (nack, ack);
  not not_5 (n0, s[0]);
  not not_6 (n1, s[1]);
  not not_7 (n2, falha_sensor);
  and and_1 (t_n, n2, n1);
  and and_2 (is_n, t_n, n0);
  and and_3 (is_v, t_n, s[0]);
  and and_4 (t_a, n2, s[1]);
  and and_5 (is_a, t_a, n0);
  and and_6 (is_c, t_a, s[0]);
  and and_7 (t_f, n1, n0);
  and and_8 (is_f, falha_sensor, t_f);
  or or_2 (o10, s[1], s[0]);
  and and_9 (inval, falha_sensor, o10);
  and and_10 (f_hold, is_f, nack);
  or or_3 (nxt[2], sf, f_hold);
  and and_11 (c_hold, is_c, nack);
  or or_4 (va, is_v, is_a);
  and and_12 (va_c, va, ge_c);
  or or_5 (x1, va_c, c_hold);
  and and_13 (nxt[1], nsf, x1);
  and and_14 (a1, is_n, ge_v);
  and and_15 (vgc, ge_v, lt_c);
  and and_16 (a2, is_v, vgc);
  or or_6 (o1, a1, a2);
  or or_7 (o2, o1, is_a);
  or or_8 (o3, o2, c_hold);
  and and_17 (nxt[0], nsf, o3);
  or or_9 (en_amostra, rst, amostra_ok);
  or or_10 (en_s, en_amostra, inval);
  not not_8 (vent, is_n);
  or or_11 (nv, is_n, is_v);
  not not_9 (alarme, nv);
  or or_12 (nva, nv, is_a);
  not not_10 (corte, nva);
  Multiplexer #(.width(3)) multiplexer_3 (.in0(nxt), .in1(3'b100), .out(s_d), .sel(inval));
  Multiplexer #(.width(3)) multiplexer_4 (.in0(s_d), .in1(3'b000), .out(multiplexer_4_out), .sel(rst));
  Register #(.width(3)) reg_s (.D(multiplexer_4_out), .en(en_s), .Q({falha_sensor, s}), .clk(clk));  // open: clr
  Multiplexer #(.width(8)) multiplexer_5 (.in0(temp), .in1({8{1'b0}}), .out(multiplexer_5_out), .sel(rst));
  Register #(.width(8)) reg_anterior (.D(multiplexer_5_out), .en(en_amostra), .Q(anterior), .clk(clk));  // open: clr
  Multiplexer #(.width(4)) multiplexer_6 (.in0({congelado, run_lo}), .in1(4'b0000), .out(multiplexer_6_out), .sel(rst));
  Register #(.width(4)) reg_run (.D(multiplexer_6_out), .en(en_amostra), .Q(run), .clk(clk));  // open: clr

  // Other names for the same wires on the sheet: alarme_o = alarme; corte_o = corte; ok = amostra_ok;
  //   run_prox[3:0] = {congelado, run_lo}; s[2] = falha_sensor; s2 = falha_sensor; vent_o = vent
endmodule

module sentinela_core (
  input  [7:0] x_in,
  input  start,
  input  ack,
  input  clk,
  input  rst,
  output [7:0] y_out,
  output done,
  output [7:0] ciclos,
  output vent,
  output alarme,
  output corte,
  output falha_sensor
);

  fir4 fir4_1 (.x_in(x_in), .start(start), .clk(clk), .rst(rst), .y_out(y_out), .done(done), .ciclos(ciclos));
  intertravamento intertravamento_1 (
    .temp(y_out), .amostra_ok(done), .ack(ack), .clk(clk), .rst(rst), .vent(vent), .alarme(alarme),
    .corte(corte), .falha_sensor(falha_sensor));

  // Other names for the same wires on the sheet: alarme_o = alarme; cic[7:0] = ciclos; corte_o = corte; dne = done;
  //   falha_o = falha_sensor; vent_o = vent; y[7:0] = y_out
endmodule
